# Fritzing sketch RoboRanger WRO Olimpiada Nacional (saved by Fritzing 0.9.10b)
breadboards: 1

parts:
  L298N1 = L298N DC motor driver
  M1 = DC Motor [voltage_(max)=6V voltage_(min)=3V]
  Part2 = Arduino Uno (Rev3) - ICSP
  J3 = Basic Servo
  J4 = Basic Servo
  U6 = LIPO-2000mAh [package=lipo-2000]
  U7 = LIPO-2000mAh [package=lipo-2000]
  U8 = LIPO-2000mAh [package=lipo-2000]
  U9 = SWITCH_SPDT [package=kps-1290]
  HC-SR04_Sensor_Delantero1 = HC-SR04 Ultrasonic Distance Sensor
  HC-SR04_Sensor_Derecho1 = HC-SR04 Ultrasonic Distance Sensor
  HC-SR04_Sensor_Izquierdo1 = HC-SR04 Ultrasonic Distance Sensor
  TCS1 = TCS3200

nets:
  N1: L298N1.OUT3, M1.pin_2
  N2: L298N1.OUT4, M1.pin_1
  VCC: L298N1.5V, Part2.VIN, J4.vcc, HC-SR04_Sensor_Delantero1.VCC, HC-SR04_Sensor_Derecho1.VCC, HC-SR04_Sensor_Izquierdo1.VCC, TCS1.VCC
  N3: L298N1.ENB, Part2.D9_PWM
  N4: L298N1.IN3, Part2.D7
  N5: L298N1.IN4, Part2.D8
  N6: Part2.A0, TCS1.S0
  N7: Part2.A1, TCS1.S1
  N8: Part2.A2, TCS1.S2
  N9: Part2.A3, TCS1.S3
  N10: Part2.A4/SDA, TCS1.OUT
  GND: Part2.GND, J3.gnd, J4.gnd, U7.-, HC-SR04_Sensor_Delantero1.GND, HC-SR04_Sensor_Derecho1.GND, HC-SR04_Sensor_Izquierdo1.GND, TCS1.GND
  N11: Part2.D10_PWM/SS, J3.pulse
  N12: Part2.D11_PWM/MOSI, HC-SR04_Sensor_Izquierdo1.ECHO
  N13: Part2.D12/MISO, HC-SR04_Sensor_Izquierdo1.TRIG
  N14: Part2.D13/SCK, TCS1.LED
  N15: Part2.D2, HC-SR04_Sensor_Derecho1.TRIG
  N16: Part2.D3_PWM, HC-SR04_Sensor_Derecho1.ECHO
  N17: Part2.D4, HC-SR04_Sensor_Delantero1.TRIG
  N18: Part2.D5_PWM, HC-SR04_Sensor_Delantero1.ECHO
  N19: Part2.D6_PWM, J4.pulse
  N20: U6.+, U9.S
  N21: U6.-, U8.+
  N22: U7.+, U8.-

notes:
  Circuito WRO nacional

custom parts:
  L298N DC motor driver: 2x DC motor driver with 78M05 positive voltage regulator (7..35 V) L298N: max 46 V, 2 A Set 5 V Enable jumper to enable 5 V regultor (needed for the L298N) and +5 V output at screw terminal or supply external +5 V at screw terminal Set ENA and/or ENB to +5 V to enable motor permanently or supply ENA and/or ENB with PWM signal IN1 and IN2 set rotation directory for motor A (OUT1/OUT2) IN2 and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
  TCS3200: COLOR SENSING TCS3200
