# Fritzing sketch Primera ronda wro (saved by Fritzing 0.9.10b)
breadboards: 1

parts:
  Puente_H_L298N = H-Bridge with L298N
  M1 = DC Motor [voltage_(max)=6V voltage_(min)=3V]
  U1 = LIPO-2000mAh [package=lipo-2000]
  U2 = LIPO-2000mAh [package=lipo-2000]
  U3 = SWITCH_SPDT [package=kps-1290]
  Part1 = Arduino Uno (Rev3) - ICSP
  HC-SR04_Sensor_Izquierdo = HC-SR04 Ultrasonic Distance Sensor
  HC-SR04_Sensor_Derecho = HC-SR04 Ultrasonic Distance Sensor
  HC-SR04_Sensor_Delantero = HC-SR04 Ultrasonic Distance Sensor
  J1 = Basic Servo

nets:
  N1: Puente_H_L298N.12V, U3.P
  N2: Puente_H_L298N.GND, U1.-
  VCC: Puente_H_L298N.5V, Part1.5V, HC-SR04_Sensor_Izquierdo.VCC, HC-SR04_Sensor_Derecho.VCC, HC-SR04_Sensor_Delantero.VCC, J1.vcc
  N3: Puente_H_L298N.M1-01, M1.pin_2
  N4: Puente_H_L298N.M1-02, Puente_H_L298N.M2-01, Puente_H_L298N.M2-02, Puente_H_L298N.ENA-5V, Puente_H_L298N.ENB-5V, M1.pin_1
  N5: U1.+, U2.-
  N6: U2.+, U3.S
  N7: Part1.D11_PWM/MOSI, HC-SR04_Sensor_Derecho.ECHO
  N8: Part1.D12/MISO, HC-SR04_Sensor_Derecho.TRIG
  GND: Part1.GND, HC-SR04_Sensor_Izquierdo.GND, HC-SR04_Sensor_Derecho.GND, HC-SR04_Sensor_Delantero.GND, J1.gnd
  N9: Part1.D2, HC-SR04_Sensor_Izquierdo.TRIG
  N10: Part1.D3_PWM, HC-SR04_Sensor_Izquierdo.ECHO
  N11: Part1.D4, HC-SR04_Sensor_Delantero.TRIG
  N12: Part1.D5_PWM, HC-SR04_Sensor_Delantero.ECHO
  N13: Part1.D6_PWM, J1.pulse

notes:
  Circuito para primera ronda WRO.

custom parts:
  H-Bridge with L298N: h-bridge
